// Digital circuit demo.dig as structural Verilog
module demo (
);

  _1bha _1bha_1 ();  // open: a, b, s, cout
  _1bha _1bha_2 ();  // open: a, b, s, cout
  _1bha _1bha_3 ();  // open: a, b, s, cout
endmodule
